# Fritzing sketch CircuitoMotorGaraje (saved by Fritzing 0.9.3b)
breadboards: 1

parts:
  Componente1 = Arduino Uno (Rev3)
  U1 = G3VM-61E1 [package=g3vm-61e1]
  U2 = G3VM-61E1 [package=g3vm-61e1]
  S1 = Toggle Switch [package=THT]
  S2 = Pushbutton [package="[THT]"]
  R1 = Resistor [tolerance=±5% resistance=10k package=THT]

nets:
  N1: Componente1.D9_PWM, U1.P$1
  N2: Componente1.D10_PWM/SS, U2.P$1
  N3: Componente1.D11_PWM/MOSI, S1.L2
  N4: Componente1.D12/MISO, S1.L1
  N5: Componente1.D2, S2.Pin_1, S2.Pin_2, R1.Pin_0
  N6: Componente1.5V, S1.COM, S2.Pin_3, S2.Pin_4
  N7: Componente1.GND, U1.P$3, U2.P$3, R1.Pin_1

// code stored in the sketch: CircuitoMotorGaraje.ino

/**
  @file CircuitoMotorGaraje.ino
  @brief Controlador del motor de la puerta del garaje
  @author Pablo Rocamora pablojoserocamora@gmail.com
  @date 11/06/2018
*/

#include "CircuitoMotorGaraje.h"

#define MODO_DEBUG true

void setup() {
  Serial.begin(115200);
  Serial.println();
  Serial.println("Inicio");

  pinMode(RELAY_OPEN_DOOR, OUTPUT);
  pinMode(RELAY_CLOSE_DOOR, OUTPUT);
  pinMode(IS_OPEN_DOOR, INPUT);
  pinMode(IS_CLOSE_DOOR, INPUT);
  pinMode(CLICK_BUTTON, INPUT);
}

/**
   Metodo para comprobar si hemos pulsado el boton, retorna true si se ha pulsado y false en caso contrario
   Guarda el estado en el que esta.
*/
bool isClickButton() {
  bool clicked = false;
  reading = digitalRead(CLICK_BUTTON);
  if (reading == HIGH && millis() - time > debounce) {
    state = HIGH;
    time = millis();
    clicked = true;
  }

  return clicked;
  Serial.println(clicked);

}

/**
   Metodo para obtener el pin al que hay que aplicar voltaje para accionar el rele
*/
int getPin() {
  int in = digitalRead(IS_CLOSE_DOOR);
  if (in == HIGH)
    return RELAY_OPEN_DOOR;  //8
  return RELAY_CLOSE_DOOR; //9
}

bool finCarrera(int pin) {

}

void play() {
  long inicio = millis();
  long fin = inicio + 10000; //tiempo maximo funcionando

  int pin =  getPin();
  digitalWrite(pin, HIGH);
  Serial.println( "pin: " + String(pin) + " estado: " + String(state));

  while (!finCarrera() || millis() < fin) {
    //if (isClickButton())
      //pause
    delay(100);
  }

}

void pause() {

}

void loop() {
  if (isClickButton()) {
    play();
  }

  if (isRunning) {

  }
}
